# Fritzing sketch schematic (saved by Fritzing 0.9.0b)
breadboards: 1

parts:
  MBED1 = mbed
  U1 = LCD-16X2 [package=lcd-16x2_noholes]
  Part1 = Digital Temperature Sensor Breakout - TMP102
  U2 = RJ45 Jack [package=rj45-8]
  R1 = Trimmer Potentiometer [maximum_resistance=10kΩ package=THT]

nets:
  GND: MBED1.GND, U1.VSS, U1.R_W, U1.K, Part1.GND, Part1.ADD0, R1.leg2
  N1: MBED1.pin9, Part1.SDA
  N2: MBED1.pin10, Part1.SCL
  N3: MBED1.pin15, U1.RS
  N4: MBED1.pin16, U1.E
  N5: MBED1.pin21, U1.DB4
  N6: MBED1.pin22, U1.DB5
  N7: MBED1.pin23, U1.DB6
  N8: MBED1.pin24, U1.DB7
  N9: MBED1.TD+, U2.1
  N10: MBED1.TD-, U2.2
  N11: MBED1.RD+, U2.3
  N12: MBED1.RD-, U2.6
  N13: MBED1.VU, U1.VDD
  N14: MBED1.VOUT, U1.A, Part1.V+, R1.leg1
  N15: U1.VO, R1.wiper
